# Fritzing sketch OLED_Water_DHT11 (saved by Fritzing 0.9.3b)
breadboards: 1

parts:
  part = Raspberry Pi Pico
  ssd1306-OLED = Grove OLED 128x96
  DHT11 = Humidity and Temperature Sensor DHT11
  Buzz = Grove Buzz
  RGB_LED = KY-016 RGB Full Color LED Module [package="Breakout board"]
  Water_Level_Sensor1 = Water Level Sensor

nets:
  GND: part.pin_3, part.pin_8, part.pin_13, part.pin_18, part.pin_23, part.pin_28, part.pin_33, part.pin_38, part.pin_42, ssd1306-OLED.GND, DHT11.GND_2, Buzz.GND, RGB_LED.-, Water_Level_Sensor1.GND
  N1: part.pin_4, RGB_LED.B
  N2: part.pin_5, RGB_LED.G
  N3: part.pin_6, RGB_LED.R
  N4: part.pin_7, Buzz.SIG
  N5: part.pin_29, DHT11.Data-signal
  N6: part.pin_31, ssd1306-OLED.SDA
  N7: part.pin_32, ssd1306-OLED.SCL
  N8: part.pin_34, Water_Level_Sensor1.SIG
  VCC: part.pin_36, ssd1306-OLED.VCC, DHT11.Vcc, Buzz.VCC, Water_Level_Sensor1.VCC

custom parts:
  Raspberry Pi Pico: Raspberry Pi Pico. Based around the RP2040 microcontroller the Pico is a low cost microcontroller device bringing Raspberry Pi quality, cost, and easy of use to the microcontroller space. Jan 2021, Split part in to two versions: SMD (this one) and tht. This one is single sided and uses the castellation pads to solder the module to the board (no holes, other than for the USB connector!). The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
  Humidity and Temperature Sensor DHT11: Digital relative humidity & temperature sensor DHT11
  KY-016 RGB Full Color LED Module: KY-016 Arduino full color 5mm RGB LED, different colors can be obtained by mixing the three primary colors.
  Water Level Sensor: A water level sensor. This sensor operates at 3V to 5V. The Sig (signal) pin outputs an analogue signal that is in proportion to the amount of water in contact with the sensor.
